// Logisim project BigASM.circ as structural Verilog
module BOARD_BIG_ASM (
  output out_1
);

  wire button_1_out, CLK, CLR, d_ff_1_q, not_1_out, Write, Write_ASCII;
  wire [6:0] ASCII;
  wire [7:0] counter_1_q;
  wire [23:0] Dir_INPUT, Dir_MEMORY;
  wire [31:0] INPUT, MEMORY_IN, MEMORY_OUT;

  Button button_1 (.out(button_1_out));
  Clock clock_1 (.out(CLK));
  D_Flip_Flop d_ff_1 (.clk(CLK), .D(1'b1), .Q(d_ff_1_q), .reset(button_1_out));  // open: Qn, preset, en
  D_Flip_Flop d_ff_2 (.clk(CLK), .D(d_ff_1_q), .Qn(CLR), .reset(button_1_out));  // open: Q, preset, en
  BIG_ASM big_asm_1 (
    .DATA_INPUT(INPUT), .MEMORY_IN(MEMORY_OUT), .CLK(CLK), .CLR(CLR), .DIR_INPUT(Dir_INPUT),
    .MEMORY_OUT(MEMORY_IN), .DIR_MEMORY(Dir_MEMORY), .Write_OUTPUT(Write), .ASCII(ASCII),
    .Write_ASCII(Write_ASCII), .END(out_1));
  MEMORY memory_1 (.DIR(Dir_MEMORY), .DATA_IN(MEMORY_IN), .WRITE(Write), .CLK(CLK), .CLR(CLR), .DATA_OUT(MEMORY_OUT));
  INPUT input_1 (.DIR(Dir_INPUT), .CLK(CLK), .DATA_OUT(INPUT));
  Counter counter_1 (.load(1'b0), .count(not_1_out), .Q(counter_1_q), .clk(CLK), .clr(CLR));  // open: D, carry
  not not_1 (not_1_out, out_1);
  // Probe on counter_1_q
  TTY #(.rows(32), .cols(60)) tty_1 (.data(ASCII), .clk(CLK), .we(Write_ASCII), .clr(CLR));

  // Other names for the same wires on the sheet: END = out_1

  // Notes on the sheet:
  //   COUNTER
  //   BOARD
endmodule

module INPUT (
  input  [23:0] DIR,
  input  CLK,
  output [31:0] DATA_OUT
);

  RAM #(.addrWidth(24), .dataWidth(32)) ram_1 (.addr(DIR), .data(DATA_OUT), .clk(CLK), .ld(1'b1));  // open: sel, clr
endmodule

module MEMORY (
  input  [23:0] DIR,
  input  [31:0] DATA_IN,
  input  WRITE,
  input  CLK,
  input  CLR,
  output [31:0] DATA_OUT
);

  RAM #(.addrWidth(24), .dataWidth(32), .bus("separate")) ram_1 (
    .addr(DIR), .din(DATA_IN), .data(DATA_OUT), .str(WRITE), .clk(CLK), .clr(CLR));  // open: sel, ld
endmodule

module BIG_ASM (
  input  [31:0] DATA_INPUT,
  input  [31:0] MEMORY_IN,
  input  CLK,
  input  CLR,
  output [23:0] DIR_INPUT,
  output [31:0] MEMORY_OUT,
  output [23:0] DIR_MEMORY,
  output Write_OUTPUT,
  output [6:0] ASCII,
  output Write_ASCII,
  output END
);

  wire c_u_1_out_7, c_u_1_out_8, c_u_1_out_9, c_u_1_out_10, c_u_1_out_11, c_u_1_out_12, d_ff_1_q, I__N_M_2,
       J__M, Start;
  wire [31:0] DI_K;

  D_Flip_Flop d_ff_1 (.clk(CLK), .D(1'b0), .Q(d_ff_1_q), .preset(CLR));  // open: Qn, en, reset
  C_U c_u_1 (
    .in_1(Start), .in_2(DI_K), .in_3(I__N_M_2), .in_4(J__M), .in_5(CLK), .in_6(CLR), .out_7(c_u_1_out_7),
    .out_8(c_u_1_out_8), .out_9(c_u_1_out_9), .out_10(c_u_1_out_10), .out_11(c_u_1_out_11),
    .out_12(c_u_1_out_12), .out_13(END), .out_14(ASCII), .out_15(Write_ASCII));
  D_Flip_Flop d_ff_2 (.clk(CLK), .D(d_ff_1_q), .Q(Start), .reset(CLR));  // open: Qn, preset, en
  D_P d_p_1 (
    .in_1(DATA_INPUT), .in_2(c_u_1_out_7), .in_3(c_u_1_out_8), .in_4(c_u_1_out_9), .in_5(c_u_1_out_10),
    .in_6(c_u_1_out_11), .in_7(c_u_1_out_12), .in_8(CLK), .in_9(CLR), .out_10(I__N_M_2), .out_11(J__M),
    .out_12(DI_K), .out_13(DIR_INPUT));

  assign DIR_MEMORY = {24{1'b0}};
  assign MEMORY_OUT = {32{1'b0}};
  assign Write_OUTPUT = 1'b0;

  // Other names for the same wires on the sheet: DI[31:0] = DATA_INPUT; Dir[23:0] = DIR_INPUT; MI[31:0] = MEMORY_IN;
  //   WA = Write_ASCII
endmodule

module PRINT_UDEC (
  input  [31:0] num,
  input  start,
  input  CLK,
  input  RST,
  output [6:0] ASCII,
  output Write_ASCII,
  output \end 
);

  wire _0_c, _0_n, demultiplexer_1_out0, demultiplexer_2_out0, demultiplexer_2_out1, demultiplexer_3_out0,
       demultiplexer_3_out1, IDLE_2_q, IDLE_3_q, IDLE_4_q, IDLE_q, Lc, Lc_0, Ln, Ln_0, or_1_out;
  wire [23:0] bit_extender_1_out;
  wire [31:0] c, c___1, c___1_t, divider_1_rem, memory_1_data_out, multiplexer_1_out, multiplexer_2_out,
       multiplexer_3_out, n, n___10, n___10___48;

  Multiplexer #(.width(32), .enable("false")) multiplexer_1 (
    .in0(num), .in1(n___10), .out(multiplexer_1_out), .sel(Lc_0));
  Divider #(.width(32)) divider_1 (.a(n), .b(32'ha), .out(n___10), .rem(divider_1_rem));  // open: upper
  Adder #(.width(32)) adder_1 (.a(divider_1_rem), .b(32'h30), .out(n___10___48));  // open: cin, cout
  or or_1 (or_1_out, demultiplexer_1_out0, \end );
  Register #(.width(32)) u_n (.D(multiplexer_1_out), .en(Ln), .Q(n), .clk(CLK), .clr(RST));
  D_Flip_Flop IDLE (.clk(CLK), .D(or_1_out), .Q(IDLE_q), .preset(RST));  // open: Qn, en, reset
  Demultiplexer #(.enable("false")) demultiplexer_1 (
    .out0(demultiplexer_1_out0), .out1(Ln_0), .in(IDLE_q), .sel(start));
  or or_2 (Write_ASCII, demultiplexer_3_out0, demultiplexer_2_out1);
  Multiplexer #(.width(32), .enable("false")) multiplexer_2 (
    .in0(c___1), .in1(c___1_t), .out(multiplexer_2_out), .sel(Write_ASCII));
  Adder #(.width(32)) adder_2 (.a(c), .b(32'h1), .out(c___1));  // open: cin, cout
  Subtractor #(.width(32)) subtractor_1 (.a(c), .b(32'h1), .out(c___1_t));  // open: bin, bout
  D_Flip_Flop IDLE_2 (.clk(CLK), .D(Ln_0), .Q(IDLE_2_q), .reset(RST));  // open: Qn, preset, en
  Register #(.width(32)) u_c (.D(multiplexer_2_out), .en(Lc), .Q(c), .clk(CLK), .clr(RST));
  or or_3 (Lc_0, IDLE_2_q, demultiplexer_3_out1);
  Multiplexer #(.width(32), .enable("false")) multiplexer_3 (
    .in0(c), .in1(c___1_t), .out(multiplexer_3_out), .sel(Write_ASCII));
  Comparator #(.width(32), .mode("unsigned")) comparator_1 (.a({32{1'b0}}), .b(n), .lt(_0_n));  // open: gt, eq
  Comparator #(.width(32), .mode("unsigned")) comparator_2 (.a({32{1'b0}}), .b(c), .lt(_0_c));  // open: gt, eq
  D_Flip_Flop IDLE_3 (.clk(CLK), .D(Write_ASCII), .Q(IDLE_3_q), .reset(RST));  // open: Qn, preset, en
  Demultiplexer #(.enable("false")) demultiplexer_2 (
    .out0(demultiplexer_2_out0), .out1(demultiplexer_2_out1), .in(IDLE_3_q), .sel(_0_c));
  Bit_Extender #(.in_width(32), .out_width(24)) bit_extender_1 (.in(multiplexer_3_out), .out(bit_extender_1_out));
  D_Flip_Flop IDLE_4 (.clk(CLK), .D(Lc_0), .Q(IDLE_4_q), .reset(RST));  // open: Qn, preset, en
  or or_4 (Lc, Lc_0, Write_ASCII);
  or or_5 (Ln, Ln_0, Lc_0);
  Demultiplexer #(.enable("false")) demultiplexer_3 (
    .out0(demultiplexer_3_out0), .out1(demultiplexer_3_out1), .in(IDLE_4_q), .sel(_0_n));
  D_Flip_Flop IDLE_5 (.clk(CLK), .D(demultiplexer_2_out0), .Q(\end ), .reset(RST));  // open: Qn, preset, en
  MEMORY memory_1 (
    .DIR(bit_extender_1_out), .DATA_IN(n___10___48), .WRITE(Lc_0), .CLK(CLK), .CLR(RST),
    .DATA_OUT(memory_1_data_out));
  Bit_Extender #(.in_width(32), .out_width(7)) bit_extender_2 (.in(memory_1_data_out), .out(ASCII));

  // Other names for the same wires on the sheet: Lc_1 = Write_ASCII; Sc = Write_ASCII; Ln_1 = Lc_0; Sn = Lc_0;
  //   Write = Lc_0
endmodule

module PRINT_DEC (
  input  [31:0] num,
  input  start,
  input  CLK,
  input  RST,
  output [6:0] ASCII,
  output Write_ASCII,
  output END
);

  wire demultiplexer_1_out0, demultiplexer_1_out1, demultiplexer_2_out0, demultiplexer_3_out0, end_t,
       IDLE_3_q, IDLE_q, or_1_out, or_2_out, or_3_out, S_ASCII, startUDEC, Write_ASCII_1;
  wire [6:0] ASCII_t;
  wire [31:0] multiplexer_1_out, negator_1_out;

  or or_1 (or_1_out, demultiplexer_1_out0, END);
  Negator #(.width(32)) negator_1 (.in(num), .out(negator_1_out));
  D_Flip_Flop IDLE (.clk(CLK), .D(or_1_out), .Q(IDLE_q), .preset(RST));  // open: Qn, en, reset
  Demultiplexer #(.enable("false")) demultiplexer_1 (
    .out0(demultiplexer_1_out0), .out1(demultiplexer_1_out1), .in(IDLE_q), .sel(start));
  Multiplexer #(.width(32), .enable("false")) multiplexer_1 (
    .in0(num), .in1(negator_1_out), .out(multiplexer_1_out), .sel(num[31]));
  Demultiplexer #(.enable("false")) demultiplexer_2 (
    .out0(demultiplexer_2_out0), .out1(S_ASCII), .in(demultiplexer_1_out1), .sel(num[31]));
  or or_2 (or_2_out, demultiplexer_2_out0, S_ASCII);
  D_Flip_Flop IDLE_2 (.clk(CLK), .D(or_2_out), .Q(startUDEC), .reset(RST));  // open: Qn, preset, en
  PRINT_UDEC print_udec_1 (
    .num(multiplexer_1_out), .start(startUDEC), .CLK(CLK), .RST(RST), .ASCII(ASCII_t),
    .Write_ASCII(Write_ASCII_1), .\end (end_t));
  D_Flip_Flop IDLE_3 (.clk(CLK), .D(or_3_out), .Q(IDLE_3_q), .reset(RST));  // open: Qn, preset, en
  or or_3 (or_3_out, startUDEC, demultiplexer_3_out0);
  Demultiplexer #(.enable("false")) demultiplexer_3 (
    .out0(demultiplexer_3_out0), .out1(END), .in(IDLE_3_q), .sel(end_t));
  Multiplexer #(.width(7), .enable("false")) multiplexer_2 (
    .in0(ASCII_t), .in1(7'b0101101), .out(ASCII), .sel(S_ASCII));
  or or_4 (Write_ASCII, S_ASCII, Write_ASCII_1);

  // Other names for the same wires on the sheet: sign = num[31]; Write_ASCII_0 = S_ASCII
endmodule

module TEST_PRINT (
  input  [31:0] in_1,
  output out_2
);

  wire button_1_out, button_2_out, CLK, CLR, d_ff_1_q, Write_ASCII;
  wire [6:0] ASCII;

  Button button_1 (.out(button_1_out));
  Clock clock_1 (.out(CLK));
  D_Flip_Flop d_ff_1 (.clk(CLK), .D(1'b1), .Q(d_ff_1_q), .reset(button_1_out));  // open: Qn, preset, en
  D_Flip_Flop d_ff_2 (.clk(CLK), .D(d_ff_1_q), .Qn(CLR), .reset(button_1_out));  // open: Q, preset, en
  Button button_2 (.out(button_2_out));
  PRINT_UDEC print_udec_1 ();  // open: num, start, CLK, RST, ASCII, Write_ASCII, end
  PRINT_DEC print_dec_1 (
    .num(in_1), .start(button_2_out), .CLK(CLK), .RST(CLR), .ASCII(ASCII), .Write_ASCII(Write_ASCII),
    .END(out_2));
  TTY #(.rows(32), .cols(60)) tty_1 (.data(ASCII), .clk(CLK), .we(Write_ASCII), .clr(CLR));
endmodule

module D_P (
  input  [31:0] in_1,
  input  in_2,
  input  in_3,
  input  in_4,
  input  in_5,
  input  in_6,
  input  in_7,
  input  in_8,
  input  in_9,
  output out_10,
  output out_11,
  output [31:0] out_12,
  output [23:0] out_13
);

  wire comparator_2_eq, comparator_2_lt;
  wire [31:0] adder_3_out, I_plus_plus, J, J_plus_plus, K, M, multiplexer_1_out, multiplier_1_out, N;
  wire [31:24] I;

  Adder #(.width(32)) adder_1 (.a({I, out_13}), .b(32'h1), .out(I_plus_plus));  // open: cin, cout
  Adder #(.width(32)) adder_2 (.a(J), .b(32'h1), .out(J_plus_plus));  // open: cin, cout
  Comparator #(.width(32), .mode("unsigned")) comparator_1 (.a(J), .b(M), .eq(out_11));  // open: gt, lt
  Register #(.width(32)) register_1 (.D(in_1), .en(in_2), .Q(N), .clk(in_8), .clr(in_9));
  Register #(.width(32)) register_2 (.D(in_1), .en(in_3), .Q(M), .clk(in_8), .clr(in_9));
  Register #(.width(32)) register_3 (.D(in_1), .en(in_4), .Q(K), .clk(in_8), .clr(in_9));
  Multiplier #(.width(32)) multiplier_1 (.a(M), .b(N), .out(multiplier_1_out));  // open: cin, cout
  Multiplier #(.width(32)) multiplier_2 (.a(in_1), .b(K), .out(out_12));  // open: cin, cout
  Adder #(.width(32)) adder_3 (.a(multiplier_1_out), .b(32'h2), .out(adder_3_out));  // open: cin, cout
  Multiplexer #(.width(32), .enable("false")) multiplexer_1 (
    .in0(J_plus_plus), .in1(32'h1), .out(multiplexer_1_out), .sel(in_7));
  Comparator #(.width(32), .mode("unsigned")) comparator_2 (
    .a({I, out_13}), .b(adder_3_out), .eq(comparator_2_eq), .lt(comparator_2_lt));  // open: gt
  Register #(.width(32)) register_4 (.D(I_plus_plus), .en(in_5), .Q({I, out_13}), .clk(in_8), .clr(in_9));
  Register #(.width(32)) register_5 (.D(multiplexer_1_out), .en(in_6), .Q(J), .clk(in_8), .clr(in_9));
  or or_1 (out_10, comparator_2_eq, comparator_2_lt);

  // Other names for the same wires on the sheet: CLK = in_8; CLR = in_9; DI[31:0] = in_1; I[23:0] = out_13;
  //   I__N_M_2 = out_10; J__M = out_11; K_DI[31:0] = out_12; LI = in_5; LJ = in_6; LK = in_4; LM = in_3; LN = in_2;
  //   SJ = in_7
endmodule

module C_U (
  input  in_1,
  input  [31:0] in_2,
  input  in_3,
  input  in_4,
  input  in_5,
  input  in_6,
  output out_7,
  output out_8,
  output out_9,
  output out_10,
  output out_11,
  output out_12,
  output out_13,
  output [6:0] out_14,
  output out_15
);

  wire Comma, demultiplexer_1_out0, demultiplexer_2_out1, IDLE_q, LI_2, LI_3, LJ_2, print_dec_1_end, SJ_2,
       W_1, WAIT_q, WHILE_q;
  wire [6:0] A1, multiplexer_1_out;

  D_Flip_Flop IDLE (.clk(in_5), .D(demultiplexer_1_out0), .Q(IDLE_q), .preset(in_6));  // open: Qn, en, reset
  Demultiplexer #(.enable("false")) demultiplexer_1 (
    .out0(demultiplexer_1_out0), .out1(out_7), .in(IDLE_q), .sel(in_1));
  D_Flip_Flop WAIT (.clk(in_5), .D(out_9), .Q(WAIT_q), .reset(in_6));  // open: Qn, preset, en
  or or_1 (LI_3, WAIT_q, LJ_2);
  D_Flip_Flop WAIT_2 (.clk(in_5), .D(out_7), .Q(out_8), .reset(in_6));  // open: Qn, preset, en
  D_Flip_Flop WHILE (.clk(in_5), .D(LI_3), .Q(WHILE_q), .reset(in_6));  // open: Qn, preset, en
  Demultiplexer #(.enable("false")) demultiplexer_2 (
    .out0(out_13), .out1(demultiplexer_2_out1), .in(WHILE_q), .sel(in_3));
  D_Flip_Flop WAIT_3 (.clk(in_5), .D(out_8), .Q(LI_2), .reset(in_6));  // open: Qn, preset, en
  or or_2 (LJ_2, SJ_2, Comma);
  D_Flip_Flop WAIT_4 (.clk(in_5), .D(LI_2), .Q(out_9), .reset(in_6));  // open: Qn, preset, en
  PRINT_DEC print_dec_1 (
    .num(in_2), .start(demultiplexer_2_out1), .CLK(in_5), .RST(in_6), .ASCII(A1), .Write_ASCII(W_1),
    .END(print_dec_1_end));
  Demultiplexer #(.enable("false")) demultiplexer_3 (.out0(Comma), .out1(SJ_2), .in(print_dec_1_end), .sel(in_4));
  Multiplexer #(.width(7), .enable("false")) multiplexer_1 (
    .in0(7'b0001010), .in1(7'b0101100), .out(multiplexer_1_out), .sel(Comma));
  or or_3 (out_10, LI_3, out_8, LI_2);
  or or_4 (out_11, out_9, LJ_2);
  or or_5 (out_12, out_9, SJ_2);
  Multiplexer #(.width(7), .enable("false")) multiplexer_2 (.in0(multiplexer_1_out), .in1(A1), .out(out_14), .sel(W_1));
  or or_6 (out_15, W_1, LJ_2);

  // Other names for the same wires on the sheet: CLK = in_5; CLR = in_6; DI_K[31:0] = in_2; END = out_13;
  //   I__N_M_2 = in_3; J__M = in_4; LI_1 = out_8; LM = out_8; LN = out_7; LJ_1 = out_9; LK = out_9; SJ_1 = out_9;
  //   Start = in_1; W_2 = LJ_2
endmodule
