// Logisim project BigASM.circ as structural Verilog
module BOARD_BIG_ASM (
  output out_1
);

  wire button_1_out, CLK, CLR, d_ff_1_q, not_1_out, Write, Write_ASCII;
  wire [6:0] ASCII;
  wire [7:0] counter_1_q;
  wire [23:0] Dir_INPUT, Dir_MEMORY;
  wire [31:0] INPUT, MEMORY_IN, MEMORY_OUT;

  Button button_1 (.out(button_1_out));
  Clock clock_1 (.out(CLK));
  D_Flip_Flop d_ff_1 (.clk(CLK), .D(1'b1), .Q(d_ff_1_q), .reset(button_1_out));  // open: Qn, preset, en
  D_Flip_Flop d_ff_2 (.clk(CLK), .D(d_ff_1_q), .Qn(CLR), .reset(button_1_out));  // open: Q, preset, en
  BIG_ASM big_asm_1 (
    .DATA_INPUT(INPUT), .MEMORY_IN(MEMORY_OUT), .CLK(CLK), .CLR(CLR), .DIR_INPUT(Dir_INPUT),
    .MEMORY_OUT(MEMORY_IN), .DIR_MEMORY(Dir_MEMORY), .Write_OUTPUT(Write), .ASCII(ASCII),
    .Write_ASCII(Write_ASCII), .END(out_1));
  MEMORY memory_1 (.DIR(Dir_MEMORY), .DATA_IN(MEMORY_IN), .WRITE(Write), .CLK(CLK), .CLR(CLR), .DATA_OUT(MEMORY_OUT));
  INPUT input_1 (.DIR(Dir_INPUT), .CLK(CLK), .DATA_OUT(INPUT));
  Counter counter_1 (.load(1'b0), .count(not_1_out), .Q(counter_1_q), .clk(CLK), .clr(CLR));  // open: D, carry
  not not_1 (not_1_out, out_1);
  // Probe on counter_1_q
  TTY #(.rows(32), .cols(60)) tty_1 (.data(ASCII), .clk(CLK), .we(Write_ASCII), .clr(CLR));

  // Other names for the same wires on the sheet: END = out_1

  // Notes on the sheet:
  //   COUNTER
  //   BOARD
endmodule

module INPUT (
  input  [23:0] DIR,
  input  CLK,
  output [31:0] DATA_OUT
);

  RAM #(.addrWidth(24), .dataWidth(32)) ram_1 (.addr(DIR), .data(DATA_OUT), .clk(CLK), .ld(1'b1));  // open: sel, clr
endmodule

module MEMORY (
  input  [23:0] DIR,
  input  [31:0] DATA_IN,
  input  WRITE,
  input  CLK,
  input  CLR,
  output [31:0] DATA_OUT
);

  RAM #(.addrWidth(24), .dataWidth(32), .bus("separate")) ram_1 (
    .addr(DIR), .din(DATA_IN), .data(DATA_OUT), .str(WRITE), .clk(CLK), .clr(CLR));  // open: sel, ld
endmodule

module BIG_ASM (
  input  [31:0] DATA_INPUT,
  input  [31:0] MEMORY_IN,
  input  CLK,
  input  CLR,
  output [23:0] DIR_INPUT,
  output [31:0] MEMORY_OUT,
  output [23:0] DIR_MEMORY,
  output Write_OUTPUT,
  output [6:0] ASCII,
  output Write_ASCII,
  output END
);

  wire c_u_1_out_10, c_u_1_out_11, c_u_1_out_12, c_u_1_out_13, c_u_1_out_14, c_u_1_out_15, c_u_1_out_16,
       d_ff_1_q, I__A, J__A_B_1, J__A_B_2, K__M_J, Space, Start;
  wire [6:0] ASCII_t;
  wire [31:0] K;

  D_Flip_Flop d_ff_1 (.clk(CLK), .D(1'b0), .Q(d_ff_1_q), .preset(CLR));  // open: Qn, en, reset
  D_Flip_Flop d_ff_2 (.clk(CLK), .D(d_ff_1_q), .Q(Start), .reset(CLR));  // open: Qn, preset, en
  C_U c_u_1 (
    .in_8(CLK), .in_1(Start), .in_9(CLR), .out_10(c_u_1_out_10), .out_11(c_u_1_out_11),
    .out_12(c_u_1_out_12), .out_13(c_u_1_out_13), .out_14(c_u_1_out_14), .out_15(c_u_1_out_15),
    .out_16(c_u_1_out_16), .out_20(END), .in_2(I__A), .in_3(K__M_J), .out_17(ASCII_t), .in_4(J__A_B_1),
    .in_6(DATA_INPUT), .out_18(Write_ASCII), .in_5(J__A_B_2), .out_19(Space), .in_7(K));
  D_P d_p_1 (
    .in_1(c_u_1_out_10), .in_2(c_u_1_out_11), .in_3(c_u_1_out_12), .in_4(c_u_1_out_13), .in_5(c_u_1_out_14),
    .in_6(c_u_1_out_15), .in_7(c_u_1_out_16), .in_8(CLK), .in_9(CLR), .in_10(DATA_INPUT), .out_12(I__A),
    .out_13(K__M_J), .out_14(J__A_B_1), .out_15(J__A_B_2), .Dir_INPUT(DIR_INPUT), .out_11(K));
  Multiplexer #(.width(7), .enable("false")) multiplexer_1 (.in0(ASCII_t), .in1(7'b0100000), .out(ASCII), .sel(Space));

  assign DIR_MEMORY = {24{1'b0}};
  assign MEMORY_OUT = {32{1'b0}};
  assign Write_OUTPUT = 1'b0;

  // Other names for the same wires on the sheet: DI[31:0] = DATA_INPUT; Dir[23:0] = DIR_INPUT; Write = Write_ASCII
endmodule

module PRINT_UDEC (
  input  [31:0] num,
  input  start,
  input  CLK,
  input  RST,
  output [6:0] ASCII,
  output Write_ASCII,
  output \end 
);

  wire _0_c, _0_n, demultiplexer_1_out0, demultiplexer_2_out0, demultiplexer_2_out1, demultiplexer_3_out0,
       demultiplexer_3_out1, IDLE_2_q, IDLE_3_q, IDLE_4_q, IDLE_q, Lc, Lc_0, Ln, Ln_0, or_1_out;
  wire [23:0] bit_extender_1_out;
  wire [31:0] c, c___1, c___1_t, divider_1_rem, memory_1_data_out, multiplexer_1_out, multiplexer_2_out,
       multiplexer_3_out, n, n___10, n___10___48;

  Multiplexer #(.width(32), .enable("false")) multiplexer_1 (
    .in0(num), .in1(n___10), .out(multiplexer_1_out), .sel(Lc_0));
  Divider #(.width(32)) divider_1 (.a(n), .b(32'ha), .out(n___10), .rem(divider_1_rem));  // open: upper
  Adder #(.width(32)) adder_1 (.a(divider_1_rem), .b(32'h30), .out(n___10___48));  // open: cin, cout
  or or_1 (or_1_out, demultiplexer_1_out0, \end );
  Register #(.width(32)) u_n (.D(multiplexer_1_out), .en(Ln), .Q(n), .clk(CLK), .clr(RST));
  D_Flip_Flop IDLE (.clk(CLK), .D(or_1_out), .Q(IDLE_q), .preset(RST));  // open: Qn, en, reset
  Demultiplexer #(.enable("false")) demultiplexer_1 (
    .out0(demultiplexer_1_out0), .out1(Ln_0), .in(IDLE_q), .sel(start));
  or or_2 (Write_ASCII, demultiplexer_3_out0, demultiplexer_2_out1);
  Multiplexer #(.width(32), .enable("false")) multiplexer_2 (
    .in0(c___1), .in1(c___1_t), .out(multiplexer_2_out), .sel(Write_ASCII));
  Adder #(.width(32)) adder_2 (.a(c), .b(32'h1), .out(c___1));  // open: cin, cout
  Subtractor #(.width(32)) subtractor_1 (.a(c), .b(32'h1), .out(c___1_t));  // open: bin, bout
  D_Flip_Flop IDLE_2 (.clk(CLK), .D(Ln_0), .Q(IDLE_2_q), .reset(RST));  // open: Qn, preset, en
  Register #(.width(32)) u_c (.D(multiplexer_2_out), .en(Lc), .Q(c), .clk(CLK), .clr(RST));
  or or_3 (Lc_0, IDLE_2_q, demultiplexer_3_out1);
  Multiplexer #(.width(32), .enable("false")) multiplexer_3 (
    .in0(c), .in1(c___1_t), .out(multiplexer_3_out), .sel(Write_ASCII));
  Comparator #(.width(32), .mode("unsigned")) comparator_1 (.a({32{1'b0}}), .b(n), .lt(_0_n));  // open: gt, eq
  Comparator #(.width(32), .mode("unsigned")) comparator_2 (.a({32{1'b0}}), .b(c), .lt(_0_c));  // open: gt, eq
  D_Flip_Flop IDLE_3 (.clk(CLK), .D(Write_ASCII), .Q(IDLE_3_q), .reset(RST));  // open: Qn, preset, en
  Demultiplexer #(.enable("false")) demultiplexer_2 (
    .out0(demultiplexer_2_out0), .out1(demultiplexer_2_out1), .in(IDLE_3_q), .sel(_0_c));
  Bit_Extender #(.in_width(32), .out_width(24)) bit_extender_1 (.in(multiplexer_3_out), .out(bit_extender_1_out));
  D_Flip_Flop IDLE_4 (.clk(CLK), .D(Lc_0), .Q(IDLE_4_q), .reset(RST));  // open: Qn, preset, en
  or or_4 (Lc, Lc_0, Write_ASCII);
  or or_5 (Ln, Ln_0, Lc_0);
  Demultiplexer #(.enable("false")) demultiplexer_3 (
    .out0(demultiplexer_3_out0), .out1(demultiplexer_3_out1), .in(IDLE_4_q), .sel(_0_n));
  D_Flip_Flop IDLE_5 (.clk(CLK), .D(demultiplexer_2_out0), .Q(\end ), .reset(RST));  // open: Qn, preset, en
  MEMORY memory_1 (
    .DIR(bit_extender_1_out), .DATA_IN(n___10___48), .WRITE(Lc_0), .CLK(CLK), .CLR(RST),
    .DATA_OUT(memory_1_data_out));
  Bit_Extender #(.in_width(32), .out_width(7)) bit_extender_2 (.in(memory_1_data_out), .out(ASCII));

  // Other names for the same wires on the sheet: Lc_1 = Write_ASCII; Sc = Write_ASCII; Ln_1 = Lc_0; Sn = Lc_0;
  //   Write = Lc_0
endmodule

module PRINT_DEC (
  input  [31:0] num,
  input  start,
  input  CLK,
  input  RST,
  output [6:0] ASCII,
  output Write_ASCII,
  output END
);

  wire demultiplexer_1_out0, demultiplexer_1_out1, demultiplexer_2_out0, demultiplexer_3_out0, end_t,
       IDLE_3_q, IDLE_q, or_1_out, or_2_out, or_3_out, S_ASCII, startUDEC, Write_ASCII_1;
  wire [6:0] ASCII_t;
  wire [31:0] multiplexer_1_out, negator_1_out;

  or or_1 (or_1_out, demultiplexer_1_out0, END);
  Negator #(.width(32)) negator_1 (.in(num), .out(negator_1_out));
  D_Flip_Flop IDLE (.clk(CLK), .D(or_1_out), .Q(IDLE_q), .preset(RST));  // open: Qn, en, reset
  Demultiplexer #(.enable("false")) demultiplexer_1 (
    .out0(demultiplexer_1_out0), .out1(demultiplexer_1_out1), .in(IDLE_q), .sel(start));
  Multiplexer #(.width(32), .enable("false")) multiplexer_1 (
    .in0(num), .in1(negator_1_out), .out(multiplexer_1_out), .sel(num[31]));
  Demultiplexer #(.enable("false")) demultiplexer_2 (
    .out0(demultiplexer_2_out0), .out1(S_ASCII), .in(demultiplexer_1_out1), .sel(num[31]));
  or or_2 (or_2_out, demultiplexer_2_out0, S_ASCII);
  D_Flip_Flop IDLE_2 (.clk(CLK), .D(or_2_out), .Q(startUDEC), .reset(RST));  // open: Qn, preset, en
  PRINT_UDEC print_udec_1 (
    .num(multiplexer_1_out), .start(startUDEC), .CLK(CLK), .RST(RST), .ASCII(ASCII_t),
    .Write_ASCII(Write_ASCII_1), .\end (end_t));
  D_Flip_Flop IDLE_3 (.clk(CLK), .D(or_3_out), .Q(IDLE_3_q), .reset(RST));  // open: Qn, preset, en
  or or_3 (or_3_out, startUDEC, demultiplexer_3_out0);
  Demultiplexer #(.enable("false")) demultiplexer_3 (
    .out0(demultiplexer_3_out0), .out1(END), .in(IDLE_3_q), .sel(end_t));
  Multiplexer #(.width(7), .enable("false")) multiplexer_2 (
    .in0(ASCII_t), .in1(7'b0101101), .out(ASCII), .sel(S_ASCII));
  or or_4 (Write_ASCII, S_ASCII, Write_ASCII_1);

  // Other names for the same wires on the sheet: sign = num[31]; Write_ASCII_0 = S_ASCII
endmodule

module TEST_PRINT (
  input  [31:0] in_1,
  output out_2
);

  wire button_1_out, button_2_out, CLK, CLR, d_ff_1_q, Write_ASCII;
  wire [6:0] ASCII;

  Button button_1 (.out(button_1_out));
  Clock clock_1 (.out(CLK));
  D_Flip_Flop d_ff_1 (.clk(CLK), .D(1'b1), .Q(d_ff_1_q), .reset(button_1_out));  // open: Qn, preset, en
  D_Flip_Flop d_ff_2 (.clk(CLK), .D(d_ff_1_q), .Qn(CLR), .reset(button_1_out));  // open: Q, preset, en
  Button button_2 (.out(button_2_out));
  PRINT_UDEC print_udec_1 ();  // open: num, start, CLK, RST, ASCII, Write_ASCII, end
  PRINT_DEC print_dec_1 (
    .num(in_1), .start(button_2_out), .CLK(CLK), .RST(CLR), .ASCII(ASCII), .Write_ASCII(Write_ASCII),
    .END(out_2));
  TTY #(.rows(32), .cols(60)) tty_1 (.data(ASCII), .clk(CLK), .we(Write_ASCII), .clr(CLR));
endmodule

module D_P (
  input  in_1,
  input  in_2,
  input  in_3,
  input  in_4,
  input  in_5,
  input  in_6,
  input  in_7,
  input  in_8,
  input  in_9,
  input  [31:0] in_10,
  output [31:0] out_11,
  output out_12,
  output out_13,
  output out_14,
  output out_15,
  output [23:0] Dir_INPUT
);

  wire comparator_2_eq, comparator_2_lt;
  wire [23:0] multiplexer_3_out, multiplexer_4_out;
  wire [31:0] A, A_1, A_2, adder_4_out, adder_6_out, B, I, I_plus_plus, J, J_plus_plus, multiplexer_1_out,
       multiplexer_2_out;

  Adder #(.width(32)) adder_1 (.a(I), .b(32'h1), .out(I_plus_plus));  // open: cin, cout
  Adder #(.width(32)) adder_2 (.a(J), .b(32'h1), .out(J_plus_plus));  // open: cin, cout
  Adder #(.width(32)) adder_3 (.a(A), .b(32'h2), .out(A_2));  // open: cin, cout
  Adder #(.width(32)) adder_4 (.a(A_2), .b(B), .out(adder_4_out));  // open: cin, cout
  Register #(.width(32)) register_1 (.D(in_10), .en(in_1), .Q(A), .clk(in_8), .clr(in_9));
  Register #(.width(32)) register_2 (.D(in_10), .en(in_2), .Q(B), .clk(in_8), .clr(in_9));
  Comparator #(.width(32), .mode("unsigned")) comparator_1 (.a(adder_4_out), .b(J), .eq(out_15));  // open: gt, lt
  Comparator #(.width(32), .mode("unsigned")) comparator_2 (
    .a(I), .b(A), .eq(comparator_2_eq), .lt(comparator_2_lt));  // open: gt
  or or_1 (out_12, comparator_2_eq, comparator_2_lt);
  Comparator #(.width(32), .mode("unsigned")) comparator_3 (.a(out_11), .b(in_10), .eq(out_13));  // open: gt, lt
  Multiplexer #(.width(32), .enable("false")) multiplexer_1 (
    .in0(J_plus_plus), .in1(A_2), .out(multiplexer_1_out), .sel(in_6));
  Multiplexer #(.width(32), .enable("false")) multiplexer_2 (
    .in0(I_plus_plus), .in1(32'h1), .out(multiplexer_2_out), .sel(in_4));
  Register #(.width(32)) register_3 (.D(multiplexer_1_out), .en(in_5), .Q(J), .clk(in_8), .clr(in_9));
  Register #(.width(32)) register_4 (.D(multiplexer_2_out), .en(in_3), .Q(I), .clk(in_8), .clr(in_9));
  Adder #(.width(32)) adder_5 (.a(A), .b(32'h1), .out(A_1));  // open: cin, cout
  Adder #(.width(32)) adder_6 (.a(A_1), .b(B), .out(adder_6_out));  // open: cin, cout
  Register #(.width(32)) register_5 (.D(in_10), .en(in_7), .Q(out_11), .clk(in_8), .clr(in_9));
  Comparator #(.width(32), .mode("unsigned")) comparator_4 (.a(J), .b(adder_6_out), .eq(out_14));  // open: gt, lt
  Multiplexer #(.width(24), .enable("false")) multiplexer_3 (
    .in0(J[23:0]), .in1(I[23:0]), .out(multiplexer_3_out), .sel(in_7));
  Multiplexer #(.width(24), .enable("false")) multiplexer_4 (
    .in0(multiplexer_3_out), .in1(A_1[23:0]), .out(multiplexer_4_out), .sel(in_2));
  Multiplexer #(.width(24), .enable("false")) multiplexer_5 (
    .in0(multiplexer_4_out), .in1({24{1'b0}}), .out(Dir_INPUT), .sel(in_1));

  // Other names for the same wires on the sheet: CLK = in_8; CLR = in_9; Data_Input[31:0] = in_10; I__A = out_12;
  //   J__A_B_1 = out_14; J__A_B_2 = out_15; K[31:0] = out_11; K__M_I = out_13; LA = in_1; LB = in_2; LI = in_3;
  //   LJ = in_5; LK = in_7; SI = in_4; SJ = in_6
endmodule

module C_U (
  input  in_1,
  input  in_2,
  input  in_3,
  input  in_4,
  input  in_5,
  input  [31:0] in_6,
  input  [31:0] in_7,
  input  in_8,
  input  in_9,
  output out_10,
  output out_11,
  output out_12,
  output out_13,
  output out_14,
  output out_15,
  output out_16,
  output [6:0] out_17,
  output out_18,
  output out_19,
  output out_20
);

  wire demultiplexer_1_out0, demultiplexer_2_out0, demultiplexer_2_out1, demultiplexer_3_out0,
       demultiplexer_4_out1, demultiplexer_5_out1, IDLE_q, LI_2, Lj_2, Lj_3, or_1_out, or_4_out, Print_B,
       print_dec_1_end, print_dec_2_end, Print_Space_1, Print_Space_2, WASCII_1, WASCII_2, WHILE_2_q,
       WHILE_3_q, WHILE_q;
  wire [6:0] ASCII_1, ASCII_2;

  D_Flip_Flop IDLE (.clk(in_8), .D(demultiplexer_1_out0), .Q(IDLE_q), .preset(in_9));  // open: Qn, en, reset
  or or_1 (or_1_out, out_16, Lj_2);
  Demultiplexer #(.enable("false")) demultiplexer_1 (
    .out0(demultiplexer_1_out0), .out1(out_10), .in(IDLE_q), .sel(in_1));
  or or_2 (Lj_3, Print_B, Print_Space_2);
  D_Flip_Flop WHILE (.clk(in_8), .D(or_1_out), .Q(WHILE_q), .reset(in_9));  // open: Qn, preset, en
  Demultiplexer #(.enable("false")) demultiplexer_2 (
    .out0(demultiplexer_2_out0), .out1(demultiplexer_2_out1), .in(WHILE_q), .sel(in_3));
  D_Flip_Flop WHILE_2 (.clk(in_8), .D(Lj_3), .Q(WHILE_2_q), .reset(in_9));  // open: Qn, preset, en
  D_Flip_Flop ESPERA (.clk(in_8), .D(out_10), .Q(out_11), .reset(in_9));  // open: Qn, preset, en
  or or_3 (LI_2, demultiplexer_2_out1, Print_Space_1);
  Demultiplexer #(.enable("false")) demultiplexer_3 (
    .out0(demultiplexer_3_out0), .out1(out_20), .in(WHILE_2_q), .sel(in_5));
  or or_4 (or_4_out, out_11, LI_2);
  Demultiplexer #(.enable("false")) demultiplexer_4 (
    .out0(Lj_2), .out1(demultiplexer_4_out1), .in(demultiplexer_2_out0), .sel(in_4));
  D_Flip_Flop WHILE_3 (.clk(in_8), .D(or_4_out), .Q(WHILE_3_q), .reset(in_9));  // open: Qn, preset, en
  Demultiplexer #(.enable("false")) demultiplexer_5 (
    .out0(Print_B), .out1(demultiplexer_5_out1), .in(WHILE_3_q), .sel(in_2));
  PRINT_DEC print_dec_1 (
    .num(in_6), .start(demultiplexer_3_out0), .CLK(in_8), .RST(in_9), .ASCII(ASCII_2),
    .Write_ASCII(WASCII_2), .END(print_dec_1_end));
  D_Flip_Flop ESPERA_2 (.clk(in_8), .D(demultiplexer_5_out1), .Q(out_16), .reset(in_9));  // open: Qn, preset, en
  PRINT_DEC print_dec_2 (
    .num(in_7), .start(demultiplexer_4_out1), .CLK(in_8), .RST(in_9), .ASCII(ASCII_1),
    .Write_ASCII(WASCII_1), .END(print_dec_2_end));
  D_Flip_Flop ESPERA_3 (.clk(in_8), .D(print_dec_1_end), .Q(Print_Space_2), .reset(in_9));  // open: Qn, preset, en
  D_Flip_Flop ESPERA_4 (.clk(in_8), .D(print_dec_2_end), .Q(Print_Space_1), .reset(in_9));  // open: Qn, preset, en
  or or_5 (out_12, out_11, LI_2);
  or or_6 (out_14, out_16, Lj_3, Lj_2);
  or or_7 (out_15, out_16, Print_B);
  Multiplexer #(.width(7), .enable("false")) multiplexer_1 (.in0(ASCII_1), .in1(ASCII_2), .out(out_17), .sel(WASCII_2));
  or or_8 (out_18, WASCII_1, WASCII_2, Print_Space_1, Print_Space_2);
  or or_9 (out_19, Print_Space_1, Print_Space_2);

  assign out_13 = out_11;

  // Other names for the same wires on the sheet: CLK = in_8; CLR = in_9; DI[31:0] = in_6; END = out_20; I__A = in_2;
  //   J__A_B_1 = in_4; J__A_B_2 = in_5; K[31:0] = in_7; K__M_I = in_3; LA = out_10; LB = out_11; LI_1 = out_11;
  //   SI = out_11; Lj_1 = out_16; LK = out_16; Sj_1 = out_16; Sj_2 = Print_B; Start = in_1; WASCII_3 = Print_Space_1;
  //   WASCII_4 = Print_Space_2
endmodule
